# Fritzing sketch schema (saved by Fritzing 0.9.2b)
breadboards: 1

parts:
  VCC1 = 4 x AAA Battery Mount
  M1 = DC Motor  # not connected
  M2 = DC Motor  # not connected
  LED1 = LED - 5mm [color="Red (633nm)" package="5 mm [THT]"]
  Part2 = SRF05 Ultrasonic Rangefinder
  R1 = Resistor [tolerance=±5% resistance=220 package="2010 [SMD]"]
  OLED1 = OLED 128x64 I2C Monochrome Display
  L298N1 = L298N DC motor driver
  J2 = Piezo Speaker
  Part3 = Arduino Nano (Rev3.0)
  J3 = Basic Servo

nets:
  GND: VCC1.-, Part2.GND, R1.Pin_1, OLED1.GND, L298N1.GND, J2.pin1, Part3.GND, J3.gnd
  12V: VCC1.+, L298N1.12V, J3.vcc
  N1: LED1.cathode, R1.Pin_0, Part3.D2
  5V: Part2.VCC, OLED1.VDD, L298N1.5V, Part3.5V
  N2: Part2.Trig, Part3.D10
  N3: Part2.Echo, Part3.D4
  N4: OLED1.SCK, Part3.A5
  N5: OLED1.SDA, Part3.A4
  N6: L298N1.ENA, Part3.D6
  N7: L298N1.ENB, Part3.D5
  N8: L298N1.IN1, Part3.D12/MISO
  N9: L298N1.IN2, Part3.D11/MOSI
  N10: L298N1.IN3, Part3.D8
  N11: L298N1.IN4, Part3.D7
  N12: J2.pin2, Part3.D3
  N13: Part3.D9, J3.pulse

custom parts:
  L298N DC motor driver: 2x DC motor driver with 78M05 positive voltage regulator (7..35 V) L298N: max 46 V, 2 A Set 5 V Enable jumper to enable 5 V regultor (needed for the L298N) and +5 V output at screw terminal or supply external +5 V at screw terminal Set ENA and/or ENB to +5 V to enable motor permanently or supply ENA and/or ENB with PWM signal IN1 and IN2 set rotation directory for motor A (OUT1/OUT2) IN2 and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
